// Logisim project F6.circ as structural Verilog: 5 circuits, main circuit main
module main (
  input  EN,
  input  rst
);

  wire clk_out;
  wire [31:0] pc_1_pc_out, rom_1_data;

  Clock clk (.out(clk_out));
  PC pc_1 (.EN(EN), .clk(clk_out), .rst(rst), .PC_out(pc_1_pc_out));  // open: PC_in, PC_select
  ROM #(.addrWidth(24), .dataWidth(32)) rom_1 (.addr(pc_1_pc_out[23:0]), .data(rom_1_data));
  Controller controller_1 (
    .opcode(rom_1_data[6:0]), .funct3(rom_1_data[14:12]), .funct7(rom_1_data[31:25]));  // open: PC_select

  // Notes on the sheet:
  //   add, addi, lui, lw, lbu, sw, sb, jalr
endmodule

module PC (
  input  [31:0] PC_in,
  input  PC_select,
  input  EN,
  input  clk,
  input  rst,
  output [31:0] PC_out
);

  wire [31:0] adder_1_out, multiplexer_1_out;

  Register #(.width(32)) register_1 (.D(multiplexer_1_out), .en(EN), .clk(clk), .Q(PC_out), .clr(rst));
  Multiplexer #(.width(32)) multiplexer_1 (.in0(PC_in), .in1(adder_1_out), .out(multiplexer_1_out), .sel(PC_select));
  Adder #(.width(32)) adder_1 (.a(PC_out), .b(32'h4), .out(adder_1_out));  // open: cin, cout

  // Notes on the sheet:
  //   add, addi, lui, lw, lbu, sw, sb, jalr
endmodule

module Fetch (
);
endmodule

module Controller (
  input  [6:0] opcode,
  input  [2:0] funct3,
  input  [6:0] funct7,
  output PC_select
);
endmodule

module Registers (
);

  Register #(.width(32)) R0 ();  // open: D, en, clk, Q, clr
  Register #(.width(32)) register_1 ();  // open: D, en, clk, Q, clr
  Register #(.width(32)) register_2 ();  // open: D, en, clk, Q, clr
  Register #(.width(32)) register_3 ();  // open: D, en, clk, Q, clr
  Register #(.width(32)) register_4 ();  // open: D, en, clk, Q, clr
  Register #(.width(32)) register_5 ();  // open: D, en, clk, Q, clr
  Register #(.width(32)) register_6 ();  // open: D, en, clk, Q, clr
  Register #(.width(32)) register_7 ();  // open: D, en, clk, Q, clr
  Register #(.width(32)) register_8 ();  // open: D, en, clk, Q, clr
  Register #(.width(32)) register_9 ();  // open: D, en, clk, Q, clr
  Register #(.width(32)) register_10 ();  // open: D, en, clk, Q, clr
  Register #(.width(32)) register_11 ();  // open: D, en, clk, Q, clr
  Register #(.width(32)) register_12 ();  // open: D, en, clk, Q, clr
  Register #(.width(32)) register_13 ();  // open: D, en, clk, Q, clr
  Register #(.width(32)) register_14 ();  // open: D, en, clk, Q, clr
  Register #(.width(32)) register_15 ();  // open: D, en, clk, Q, clr
endmodule
